// Logisim project 3 bit parallel adder.circ as structural Verilog: 9 circuits, main circuit main
module main (
  output [2:0] A_O,
  output [2:0] B,
  output Carry
);

  wire A_out, Add_out, Adder_c, B_out, clock_1_out, multiplexer_3_out;
  wire [2:0] Adder_s, Counter_2_out_2, Counter_out_2, multiplexer_1_out, multiplexer_2_out;

  Button A (.out(A_out));
  Button u_B (.out(B_out));
  Button Add (.out(Add_out));
  Clock clock_1 (.out(clock_1_out));
  counter Counter (.in_1(A_out), .out_2(Counter_out_2));
  counter Counter_2 (.in_1(B_out), .out_2(Counter_2_out_2));
  Multiplexer #(.width(3), .enable("false")) multiplexer_1 (
    .in0(Counter_out_2), .in1(Adder_s), .out(multiplexer_1_out), .sel(Add_out));
  Multiplexer #(.width(3), .enable("false")) multiplexer_2 (
    .in0(Counter_2_out_2), .in1(3'b000), .out(multiplexer_2_out), .sel(Add_out));
  Register #(.width(3)) register_1 (.D(multiplexer_1_out), .Q(A_O), .clk(clock_1_out));  // open: en, clr
  Register #(.width(3)) register_2 (.D(multiplexer_2_out), .Q(B), .clk(clock_1_out));  // open: en, clr
  _4_bit_parallel_adder Adder (.A(A_O), .B(B), .C(Adder_c), .S(Adder_s));
  Multiplexer #(.enable("false")) multiplexer_3 (.in0(Adder_c), .in1(Carry), .out(multiplexer_3_out), .sel(Add_out));
  D_flipflop D_flip (.in_2(multiplexer_3_out), .out_3(Carry), .in_1(clock_1_out));
endmodule

module _4_bit_parallel_adder (
  input  [2:0] A,
  input  [2:0] B,
  output [2:0] S,
  output C
);

  wire full_adder_1_c, half_adder_1_c;

  Full_adder full_adder_1 (.C(full_adder_1_c), .A(B[1]), .B(A[1]), .S(S[1]), .C0(half_adder_1_c));
  Full_adder full_adder_2 (.C(C), .A(B[2]), .B(A[2]), .S(S[2]), .C0(full_adder_1_c));
  Half_adder half_adder_1 (.A(B[0]), .B(A[0]), .S(S[0]), .C(half_adder_1_c));
endmodule

// Adder
module Full_adder (
  input  A,
  input  B,
  input  C0,
  output C,
  output S
);

  wire half_adder_1_c, half_adder_1_s, half_adder_2_c, nand_2_out, nand_3_out;

  nand nand_1 (C, nand_2_out, nand_3_out);
  nand nand_2 (nand_2_out, half_adder_1_c, half_adder_1_c);
  nand nand_3 (nand_3_out, half_adder_2_c, half_adder_2_c);
  Half_adder half_adder_1 (.A(A), .B(B), .S(half_adder_1_s), .C(half_adder_1_c));
  Half_adder half_adder_2 (.A(half_adder_1_s), .B(C0), .S(S), .C(half_adder_2_c));
endmodule

module Half_adder (
  input  A,
  input  B,
  output S,
  output C
);

  wire nand_1_out, nand_2_out, nand_4_out;

  nand nand_1 (nand_1_out, A, nand_2_out);
  nand nand_2 (nand_2_out, A, B);
  nand nand_3 (C, nand_2_out, nand_2_out);
  nand nand_4 (nand_4_out, nand_2_out, B);
  nand nand_5 (S, nand_1_out, nand_4_out);
endmodule

module counter (
  input  in_1,
  output [2:0] out_2
);

  wire j_k_ff_1_qn, j_k_ff_2_qn;

  J_K_Flip_Flop j_k_ff_1 (.J(1'b1), .clk(in_1), .K(1'b1), .Q(out_2[0]), .Qn(j_k_ff_1_qn));  // open: preset, en, reset
  J_K_Flip_Flop j_k_ff_2 (
    .J(1'b1), .clk(j_k_ff_1_qn), .K(1'b1), .Q(out_2[1]), .Qn(j_k_ff_2_qn));  // open: preset, en, reset
  J_K_Flip_Flop j_k_ff_3 (.J(1'b1), .clk(j_k_ff_2_qn), .K(1'b1), .Q(out_2[2]));  // open: Qn, preset, en, reset
endmodule

module D_flipflop (
  input  in_1,
  input  in_2,
  output out_3
);

  wire nand_1_out, nand_2_out, nand_3_out, nand_4_out, Rising_edge_checker_out_2;

  Rising_edge_checker Rising_edge_checker (.in_1(in_1), .out_2(Rising_edge_checker_out_2));
  nand nand_1 (nand_1_out, in_2, in_2);
  nand nand_2 (nand_2_out, nand_1_out, Rising_edge_checker_out_2);
  nand nand_3 (nand_3_out, Rising_edge_checker_out_2, in_2);
  nand nand_4 (nand_4_out, nand_2_out, out_3);
  nand nand_5 (out_3, nand_4_out, nand_3_out);
endmodule

module Rising_edge_checker (
  input  in_1,
  output out_2
);

  wire nand_1_out, nand_2_out, nand_3_out;

  nand nand_1 (nand_1_out, in_1, in_1);
  nand nand_2 (nand_2_out, nand_1_out, nand_1_out);
  nand nand_3 (nand_3_out, nand_2_out, nand_2_out);
  And and_1 (.in_1(in_1), .in_2(nand_3_out), .out_3(out_2));
endmodule

// XOR
module \xor  (
  input  in_1,
  input  in_2,
  output out_3
);

  wire nand_1_out, nand_2_out, nand_3_out;

  nand nand_1 (nand_1_out, in_1, nand_2_out);
  nand nand_2 (nand_2_out, in_1, in_2);
  nand nand_3 (nand_3_out, nand_2_out, in_2);
  nand nand_4 (out_3, nand_1_out, nand_3_out);
endmodule

// AND
module And (
  input  in_1,
  input  in_2,
  output out_3
);

  wire nand_1_out;

  nand nand_1 (nand_1_out, in_1, in_2);
  nand nand_2 (out_3, nand_1_out, nand_1_out);
endmodule
