// Logisim project 3 bit parallel in sirial out shift register.circ as structural Verilog: 1 circuit, main circuit main
module main (
  input  a2,
  input  a1,
  input  a0,
  input  shift,
  input  clk,
  input  rst,
  output \output 
);

  wire d_ff_1_q, d_ff_2_q, main_1_a_complement, main_2_a_b, main_3_a_b, main_4_a_b, main_5_a_b, main_6_a_b,
       main_7_a_b;

  NOT_using_NAND_main main_1 (.a(shift), .a_complement(main_1_a_complement));
  D_Flip_Flop d_ff_1 (.clk(clk), .D(a2), .Q(d_ff_1_q), .reset(rst));  // open: Qn, preset, en
  AND_using_NAND_main main_2 (.a(shift), .b(d_ff_1_q), .a_b(main_2_a_b));
  OR_gate_using_NAND_gate_main main_3 (.a(main_4_a_b), .b(main_2_a_b), .a_b(main_3_a_b));
  AND_using_NAND_main main_4 (.a(a1), .b(main_1_a_complement), .a_b(main_4_a_b));
  D_Flip_Flop d_ff_2 (.clk(clk), .D(main_3_a_b), .Q(d_ff_2_q), .reset(rst));  // open: Qn, preset, en
  AND_using_NAND_main main_5 (.a(a0), .b(main_1_a_complement), .a_b(main_5_a_b));
  AND_using_NAND_main main_6 (.a(shift), .b(d_ff_2_q), .a_b(main_6_a_b));
  OR_gate_using_NAND_gate_main main_7 (.a(main_5_a_b), .b(main_6_a_b), .a_b(main_7_a_b));
  D_Flip_Flop d_ff_3 (.clk(clk), .D(main_7_a_b), .Q(\output ), .reset(rst));  // open: Qn, preset, en

  // Notes on the sheet:
  //   3-bit parallel in serial out register
endmodule
