// Logisim project 3 bit register.circ as structural Verilog: 1 circuit, main circuit main
// a0
module main (
  input  a2,
  input  a1,
  input  a0,
  input  clk,
  output o0,
  output o1,
  output o2
);

  D_Flip_Flop d_ff_1 (.clk(clk), .D(a0), .Q(o0));  // open: Qn, preset, en, reset
  D_Flip_Flop d_ff_2 (.clk(clk), .D(a1), .Q(o1));  // open: Qn, preset, en, reset
  D_Flip_Flop d_ff_3 (.clk(clk), .D(a2), .Q(o2));  // open: Qn, preset, en, reset

  // Notes on the sheet:
  //   3-bit parallel in parallel out register
endmodule
