// Logisim project 3 bit sirial in parallel out register.circ as structural Verilog: 1 circuit, main circuit main
module main (
  input  \input ,
  input  clock,
  input  reset,
  output s2,
  output s1,
  output s0
);

  D_Flip_Flop d_ff_1 (.clk(clock), .D(\input ), .Q(s2), .reset(reset));  // open: Qn, preset, en
  D_Flip_Flop d_ff_2 (.clk(clock), .D(s2), .Q(s1), .reset(reset));  // open: Qn, preset, en
  D_Flip_Flop d_ff_3 (.clk(clock), .D(s1), .Q(s0), .reset(reset));  // open: Qn, preset, en

  // Notes on the sheet:
  //   3-bit serial in parallel out register
endmodule
