// Logisim project 3bitcounter.circ as structural Verilog: 1 circuit, main circuit main
module main (
  input  load,
  input  clock,
  input  reset,
  output a2,
  output a1,
  output a0
);

  wire j_k_ff_1_q, j_k_ff_2_q;

  J_K_Flip_Flop j_k_ff_1 (.J(load), .clk(clock), .K(load), .Q(j_k_ff_1_q), .Qn(a0), .reset(reset));  // open: preset, en
  J_K_Flip_Flop j_k_ff_2 (
    .J(load), .clk(j_k_ff_1_q), .K(load), .Q(j_k_ff_2_q), .Qn(a1), .reset(reset));  // open: preset, en
  J_K_Flip_Flop j_k_ff_3 (.J(load), .clk(j_k_ff_2_q), .K(load), .Qn(a2), .reset(reset));  // open: Q, preset, en

  // Notes on the sheet:
  //   3-bit  counter
endmodule
