// Logisim project 41MUX.circ as structural Verilog: 1 circuit, main circuit main
module main (
  input  I0,
  input  I1,
  input  I2,
  input  I3,
  input  S1,
  input  S0,
  output OUT
);

  wire nand_1_out, nand_2_out, nand_3_out, nand_4_out, nand_5_out, nand_6_out, nand_7_out, nand_8_out,
       nand_9_out, nand_10_out;

  nand nand_1 (nand_1_out, S1, S1);
  nand nand_2 (nand_2_out, S0, S0);
  nand nand_3 (nand_3_out, I0, nand_2_out);
  nand nand_4 (nand_4_out, nand_3_out, nand_5_out);
  nand nand_5 (nand_5_out, I1, S0);
  nand nand_6 (nand_6_out, I2, nand_2_out);
  nand nand_7 (nand_7_out, nand_6_out, nand_8_out);
  nand nand_8 (nand_8_out, I3, S0);
  nand nand_9 (nand_9_out, nand_4_out, nand_1_out);
  nand nand_10 (nand_10_out, S1, nand_7_out);
  nand nand_11 (OUT, nand_9_out, nand_10_out);
endmodule
