// Logisim project 7 segment display decoder.circ as structural Verilog: 1 circuit, main circuit main
module main (
  input  A,
  input  B,
  input  c,
  input  D,
  output a_2,
  output b_2,
  output c_2,
  output d_2,
  output e,
  output f,
  output g
);

  wire and_1_out, and_3_out, and_4_out, and_5_out, not_1_out, not_2_out, not_3_out, not_4_out, or_2_out,
       or_3_out, or_4_out, xnor_1_out, xnor_2_out, xor_1_out, xor_2_out;

  not not_1 (not_1_out, A);
  not not_2 (not_2_out, B);
  not not_3 (not_3_out, c);
  not not_4 (not_4_out, D);
  xnor xnor_1 (xnor_1_out, B, D);
  xnor xnor_2 (xnor_2_out, c, D);
  or or_1 (c_2, B, not_3_out, D);
  or or_2 (or_2_out, c, not_4_out);
  and and_1 (and_1_out, c, not_4_out);
  or or_3 (or_3_out, not_2_out, c);
  or or_4 (or_4_out, not_3_out, not_4_out);
  xor xor_1 (xor_1_out, B, c);
  and and_2 (e, or_3_out, not_4_out);
  and and_3 (and_3_out, or_4_out, B);
  and and_4 (and_4_out, not_3_out, not_4_out);
  and and_5 (and_5_out, c, not_4_out);
  or or_5 (a_2, xnor_1_out, A, c);
  or or_6 (b_2, xnor_2_out, not_2_out);
  xor xor_2 (xor_2_out, or_2_out, B);
  or or_7 (d_2, xor_2_out, and_1_out, A);
  or or_8 (f, and_3_out, and_4_out, A);
  or or_9 (g, xor_1_out, and_5_out, A);
  _7_Segment_Display u_7_segment_display_1 (.g(g), .f(f), .a(a_2), .b(b_2), .e(e), .d(d_2), .c(c_2));  // open: dp
endmodule
