// Logisim project AND using NAND.circ as structural Verilog: 1 circuit, main circuit main
module main (
  input  a,
  input  b,
  output a_b
);

  wire nand_1_out;

  nand nand_1 (nand_1_out, a, b);
  nand nand_2 (a_b, nand_1_out, nand_1_out);
endmodule
