// Logisim project DECADE.circ as structural Verilog: 1 circuit, main circuit main
module main (
  input  [3:0] load_signal,
  input  lode,
  input  clk,
  input  reset_key,
  output a3,
  output a2,
  output a1,
  output a0
);

  wire and_1_out, and_2_out, and_3_out, and_4_out, j_k_ff_4_qn, main_1_a_2, main_1_b_2, main_1_c_2,
       main_1_d_2, main_1_e, main_1_f, main_1_g, multiplexer_1_out, multiplexer_2_out, multiplexer_3_out,
       multiplexer_4_out, or_1_out;

  Multiplexer #(.enable("false")) multiplexer_1 (.in0(1'b1), .in1(load_signal[0]), .out(multiplexer_1_out), .sel(lode));
  J_K_Flip_Flop #(.trigger("falling")) j_k_ff_1 (
    .J(multiplexer_1_out), .clk(clk), .K(multiplexer_1_out), .Q(a0), .reset(reset_key));  // open: Qn, preset, en
  and and_1 (and_1_out, a0, j_k_ff_4_qn);
  Multiplexer #(.enable("false")) multiplexer_2 (
    .in0(and_1_out), .in1(load_signal[1]), .out(multiplexer_2_out), .sel(lode));
  J_K_Flip_Flop #(.trigger("falling")) j_k_ff_2 (
    .J(multiplexer_2_out), .clk(clk), .K(multiplexer_2_out), .Q(a1), .reset(reset_key));  // open: Qn, preset, en
  and and_2 (and_2_out, a0, a1);
  Multiplexer #(.enable("false")) multiplexer_3 (
    .in0(and_2_out), .in1(load_signal[2]), .out(multiplexer_3_out), .sel(lode));
  J_K_Flip_Flop #(.trigger("falling")) j_k_ff_3 (
    .J(multiplexer_3_out), .clk(clk), .K(multiplexer_3_out), .Q(a2), .reset(reset_key));  // open: Qn, preset, en
  Multiplexer #(.enable("false")) multiplexer_4 (
    .in0(or_1_out), .in1(load_signal[3]), .out(multiplexer_4_out), .sel(lode));
  and and_3 (and_3_out, and_2_out, a2);
  and and_4 (and_4_out, a0, a3);
  or or_1 (or_1_out, and_3_out, and_4_out);
  _7_segment_display_decoder_main main_1 (
    .A(a3), .B(a2), .c(a1), .D(a0), .a_2(main_1_a_2), .b_2(main_1_b_2), .c_2(main_1_c_2), .d_2(main_1_d_2),
    .e(main_1_e), .f(main_1_f), .g(main_1_g));
  J_K_Flip_Flop #(.trigger("falling")) j_k_ff_4 (
    .J(multiplexer_4_out), .clk(clk), .K(multiplexer_4_out), .Q(a3), .Qn(j_k_ff_4_qn), .reset(reset_key));  // open: preset, en
  _7_Segment_Display u_7_segment_display_1 (
    .g(main_1_g), .f(main_1_f), .a(main_1_a_2), .b(main_1_b_2), .e(main_1_e), .d(main_1_d_2), .c(main_1_c_2));  // open: dp
endmodule
