// Logisim project ODD PARITY.circ as structural Verilog: 2 circuits, main circuit main
module main (
  input  A,
  input  B,
  input  C,
  output O
);

  wire xor_1_out_3, xor_2_out_3;

  XOR xor_1 (.A(A), .B(B), .out_3(xor_1_out_3));
  XOR xor_2 (.A(xor_1_out_3), .B(C), .out_3(xor_2_out_3));
  nand nand_1 (O, xor_2_out_3, xor_2_out_3);
endmodule

module XOR (
  input  A,
  input  B,
  output out_3
);

  wire nand_1_out, nand_2_out, nand_3_out;

  nand nand_1 (nand_1_out, A, B);
  nand nand_2 (nand_2_out, A, nand_1_out);
  nand nand_3 (nand_3_out, nand_1_out, B);
  nand nand_4 (out_3, nand_2_out, nand_3_out);
endmodule
