// Logisim project Series adder.circ as structural Verilog: 8 circuits, main circuit serial adder
module serial_adder (
  input  ADD,
  output [3:0] A,
  output Carry,
  output [3:0] B,
  output [1:0] Pulse_count
);

  wire A_out, B_out, clock_1_out, full_adder_1_c, full_adder_1_s, multiplexer_1_out, multiplexer_2_out,
       multiplexer_3_out, multiplexer_4_out, multiplexer_5_out, shift_register_1_out, shift_register_2_out;

  Button u_A (.out(A_out));
  Button u_B (.out(B_out));
  counter Counter (.in_1(A_out), .out_2(A));
  counter Counter_2 (.in_1(B_out), .out_2(B));
  Clock clock_1 (.out(clock_1_out));
  _2bit_counter _2bit (.in_1(clock_1_out), .out_2(Pulse_count));
  Multiplexer #(.select(2), .enable("false")) multiplexer_1 (
    .in0(A[0]), .in1(A[1]), .in2(A[2]), .in3(A[3]), .out(multiplexer_1_out), .sel(Pulse_count));
  Multiplexer #(.select(2), .enable("false")) multiplexer_2 (
    .in0(B[0]), .in1(B[1]), .in2(B[2]), .in3(B[3]), .out(multiplexer_2_out), .sel(Pulse_count));
  Multiplexer #(.enable("false")) multiplexer_3 (
    .in0(multiplexer_1_out), .in1(full_adder_1_s), .out(multiplexer_3_out), .sel(ADD));
  Multiplexer #(.enable("false")) multiplexer_4 (
    .in0(multiplexer_2_out), .in1(1'b0), .out(multiplexer_4_out), .sel(ADD));
  Shift_Register #(.length(4)) shift_register_1 (
    .in(multiplexer_3_out), .clk(clock_1_out), .out(shift_register_1_out));  // open: shift, load, clr, d0, q0, d1, q1, d2, q2, d3, q3
  Shift_Register #(.length(4)) shift_register_2 (
    .in(multiplexer_4_out), .clk(clock_1_out), .out(shift_register_2_out));  // open: shift, load, clr, d0, q0, d1, q1, d2, q2, d3, q3
  Full_adder full_adder_1 (
    .C(full_adder_1_c), .A(shift_register_2_out), .B(shift_register_1_out), .S(full_adder_1_s),
    .C0(multiplexer_5_out));
  Multiplexer #(.select(2), .enable("false")) multiplexer_5 (
    .in0(1'b0), .in1(Carry), .in2(Carry), .in3(Carry), .out(multiplexer_5_out), .sel(Pulse_count));
  D_flipflop d_flipflop_1 (.in_2(full_adder_1_c), .out_3(Carry), .in_1(clock_1_out));
endmodule

// Adder
module Full_adder (
  input  A,
  input  B,
  input  C0,
  output C,
  output S
);

  wire half_adder_1_c, half_adder_1_s, half_adder_2_c, nand_2_out, nand_3_out;

  nand nand_1 (C, nand_2_out, nand_3_out);
  nand nand_2 (nand_2_out, half_adder_1_c, half_adder_1_c);
  nand nand_3 (nand_3_out, half_adder_2_c, half_adder_2_c);
  Half_adder half_adder_1 (.A(A), .B(B), .S(half_adder_1_s), .C(half_adder_1_c));
  Half_adder half_adder_2 (.A(half_adder_1_s), .B(C0), .S(S), .C(half_adder_2_c));
endmodule

module Half_adder (
  input  A,
  input  B,
  output S,
  output C
);

  wire nand_1_out, nand_2_out, nand_3_out;

  nand nand_1 (nand_1_out, A, nand_2_out);
  nand nand_2 (nand_2_out, A, B);
  nand nand_3 (nand_3_out, nand_2_out, B);
  nand nand_4 (C, nand_2_out, nand_2_out);
  nand nand_5 (S, nand_1_out, nand_3_out);
endmodule

module counter (
  input  in_1,
  output [3:0] out_2
);

  wire j_k_ff_1_qn, j_k_ff_2_qn, j_k_ff_3_qn;

  J_K_Flip_Flop j_k_ff_1 (.J(1'b1), .clk(in_1), .K(1'b1), .Q(out_2[0]), .Qn(j_k_ff_1_qn));  // open: preset, en, reset
  J_K_Flip_Flop j_k_ff_2 (
    .J(1'b1), .clk(j_k_ff_1_qn), .K(1'b1), .Q(out_2[1]), .Qn(j_k_ff_2_qn));  // open: preset, en, reset
  J_K_Flip_Flop j_k_ff_3 (
    .J(1'b1), .clk(j_k_ff_2_qn), .K(1'b1), .Q(out_2[2]), .Qn(j_k_ff_3_qn));  // open: preset, en, reset
  J_K_Flip_Flop j_k_ff_4 (.J(1'b1), .clk(j_k_ff_3_qn), .K(1'b1), .Q(out_2[3]));  // open: Qn, preset, en, reset
endmodule

module _2bit_counter (
  input  in_1,
  output [1:0] out_2
);

  wire j_k_ff_1_qn;

  J_K_Flip_Flop j_k_ff_1 (.J(1'b1), .clk(in_1), .K(1'b1), .Q(out_2[0]), .Qn(j_k_ff_1_qn));  // open: preset, en, reset
  J_K_Flip_Flop j_k_ff_2 (.J(1'b1), .clk(j_k_ff_1_qn), .K(1'b1), .Q(out_2[1]));  // open: Qn, preset, en, reset
endmodule

// D
module D_flipflop (
  input  in_1,
  input  in_2,
  output out_3
);

  wire nand_1_out, nand_2_out, nand_3_out, nand_4_out, Rising_edge_checker_out_2;

  Rising_edge_checker Rising_edge_checker (.in_1(in_1), .out_2(Rising_edge_checker_out_2));
  nand nand_1 (nand_1_out, in_2, in_2);
  nand nand_2 (nand_2_out, nand_1_out, Rising_edge_checker_out_2);
  nand nand_3 (nand_3_out, Rising_edge_checker_out_2, in_2);
  nand nand_4 (nand_4_out, nand_2_out, out_3);
  nand nand_5 (out_3, nand_4_out, nand_3_out);
endmodule

module Rising_edge_checker (
  input  in_1,
  output out_2
);

  wire nand_1_out, nand_2_out, nand_3_out;

  nand nand_1 (nand_1_out, in_1, in_1);
  nand nand_2 (nand_2_out, nand_1_out, nand_1_out);
  nand nand_3 (nand_3_out, nand_2_out, nand_2_out);
  And and_1 (.in_1(in_1), .in_2(nand_3_out), .out_3(out_2));
endmodule

// AND
module And (
  input  in_1,
  input  in_2,
  output out_3
);

  wire nand_1_out;

  nand nand_1 (nand_1_out, in_1, in_2);
  nand nand_2 (out_3, nand_1_out, nand_1_out);
endmodule
