// Logisim project binary to bcd encoader.circ as structural Verilog: 1 circuit, main circuit main
module main (
  input  A,
  input  B,
  input  C,
  input  D,
  output b8,
  output b7,
  output b6,
  output b5,
  output b4,
  output b3,
  output b2,
  output b1
);

  wire and_1_out, and_2_out, and_3_out, and_4_out, not_1_out, not_2_out, not_3_out, not_4_out, or_1_out;

  not not_1 (not_1_out, A);
  not not_2 (not_2_out, B);
  not not_3 (not_3_out, C);
  not not_4 (not_4_out, D);
  and and_1 (and_1_out, A, B);
  and and_2 (and_2_out, A, C);
  or or_1 (or_1_out, not_1_out, C);
  and and_3 (and_3_out, A, B, not_3_out);
  and and_4 (and_4_out, not_1_out, C);
  and and_5 (b3, or_1_out, B);
  or or_2 (b5, and_1_out, and_2_out);
  and and_6 (b4, A, not_2_out, not_3_out);
  or or_3 (b2, and_3_out, and_4_out);

  assign b1 = D;
  assign b6 = 1'b0;
  assign b7 = 1'b0;
  assign b8 = 1'b0;
endmodule
