// Logisim project c1.circ as structural Verilog: 1 circuit, main circuit main
module main (
  input  A,
  input  B,
  output Y_AB_prime_A_prime_B
);

  wire and_1_out, and_2_out, not_1_out, not_2_out;

  not not_1 (not_1_out, B);
  not not_2 (not_2_out, A);
  and and_1 (and_1_out, A, not_1_out);
  and and_2 (and_2_out, B, not_2_out);
  or or_1 (Y_AB_prime_A_prime_B, and_1_out, and_2_out);

  // Notes on the sheet:
  //   A
  //   B'
  //   B
  //   A'
  //   AB'
  //   A'B
endmodule
