// Logisim project c3.circ as structural Verilog: 1 circuit, main circuit main
module main (
  input  a,
  input  b,
  input  c,
  input  d,
  output \output 
);

  wire nand_1_out, nand_2_out, nand_3_out, nand_4_out, nand_5_out, nand_6_out;

  nand nand_1 (nand_1_out, a, b);
  nand nand_2 (nand_2_out, b, c);
  nand nand_3 (nand_3_out, c, d);
  nand nand_4 (nand_4_out, d, a);
  nand nand_5 (nand_5_out, nand_1_out, nand_2_out);
  nand nand_6 (nand_6_out, nand_3_out, nand_4_out);
  nand nand_7 (\output , nand_5_out, nand_6_out);

  // Notes on the sheet:
  //   (a.b)'
  //   (b.c)'
  //   (c.d)'
  //   (d.a)'
  //   ((a.b)'.(b.c)')'=ab+bc
  //           ((c.d)'.(d.a)')'=cd+da
  //   =b'+d'+a'.c'
endmodule
