// Logisim project counter up+down.circ as structural Verilog: 1 circuit, main circuit main
module main (
  input  in_1,
  input  in_2,
  output out_3,
  output out_4,
  output out_5
);

  wire and_1_out, and_2_out, and_3_out, and_4_out, and_5_out, and_6_out, clock_1_out, j_k_ff_1_q,
       j_k_ff_1_qn, j_k_ff_2_q, j_k_ff_2_qn, j_k_ff_3_q, j_k_ff_3_qn, not_1_out;

  Clock clock_1 (.out(clock_1_out));
  not not_1 (not_1_out, in_1);
  J_K_Flip_Flop #(.trigger("falling")) j_k_ff_1 (
    .J(in_2), .clk(clock_1_out), .K(in_2), .Q(j_k_ff_1_q), .Qn(j_k_ff_1_qn));  // open: preset, en, reset
  and and_1 (and_1_out, j_k_ff_1_q, in_1);
  or or_1 (out_5, and_1_out, and_2_out);
  J_K_Flip_Flop #(.trigger("falling")) j_k_ff_2 (
    .J(in_2), .clk(j_k_ff_1_q), .K(in_2), .Q(j_k_ff_2_q), .Qn(j_k_ff_2_qn));  // open: preset, en, reset
  and and_2 (and_2_out, not_1_out, j_k_ff_1_qn);
  and and_3 (and_3_out, j_k_ff_2_q, in_1);
  and and_4 (and_4_out, not_1_out, j_k_ff_2_qn);
  or or_2 (out_4, and_3_out, and_4_out);
  J_K_Flip_Flop #(.trigger("falling")) j_k_ff_3 (
    .J(in_2), .clk(j_k_ff_2_q), .K(in_2), .Q(j_k_ff_3_q), .Qn(j_k_ff_3_qn));  // open: preset, en, reset
  and and_5 (and_5_out, j_k_ff_3_q, in_1);
  and and_6 (and_6_out, j_k_ff_3_qn, not_1_out);
  or or_3 (out_3, and_5_out, and_6_out);
endmodule
