// Logisim project full adder-exam.circ as structural Verilog: 1 circuit, main circuit main
module main (
  input  a,
  input  b,
  input  carry_in,
  output sum,
  output carry_out
);

  wire nand_1_out, nand_2_out, nand_3_out, nand_4_out, nand_5_out, nand_6_out, nand_7_out, nand_8_out,
       nand_9_out, nand_10_out, nand_12_out, nand_13_out, nand_14_out;

  nand nand_1 (nand_1_out, a, b);
  nand nand_2 (nand_2_out, a, nand_1_out);
  nand nand_3 (nand_3_out, nand_1_out, b);
  nand nand_4 (nand_4_out, nand_2_out, nand_3_out);
  nand nand_5 (nand_5_out, nand_4_out, carry_in);
  nand nand_6 (nand_6_out, nand_4_out, nand_5_out);
  nand nand_7 (nand_7_out, nand_5_out, carry_in);
  nand nand_8 (nand_8_out, nand_4_out, carry_in);
  nand nand_9 (nand_9_out, b, a);
  nand nand_10 (nand_10_out, nand_8_out, nand_8_out);
  nand nand_11 (sum, nand_6_out, nand_7_out);
  nand nand_12 (nand_12_out, nand_9_out, nand_9_out);
  nand nand_13 (nand_13_out, nand_10_out, nand_10_out);
  nand nand_14 (nand_14_out, nand_12_out, nand_12_out);
  nand nand_15 (carry_out, nand_13_out, nand_14_out);
endmodule
