// Logisim project half adder-exam.circ as structural Verilog: 1 circuit, main circuit main
module main (
  input  a,
  input  b,
  output sum,
  output carry
);

  wire nand_1_out, nand_2_out, nand_3_out, nand_4_out;

  nand nand_1 (nand_1_out, a, b);
  nand nand_2 (nand_2_out, a, nand_1_out);
  nand nand_3 (nand_3_out, nand_1_out, b);
  nand nand_4 (nand_4_out, a, b);
  nand nand_5 (sum, nand_2_out, nand_3_out);
  nand nand_6 (carry, nand_4_out, nand_4_out);
endmodule
