// Logisim project lab assgnment.circ as structural Verilog: 1 circuit, main circuit main
module main (
  input  a3,
  input  a2,
  input  a1,
  input  a0,
  output \output 
);

  wire main_1_out_4, main_2_out_4, nand_1_out, nand_2_out, nand_3_out, nand_4_out, nand_5_out, nand_6_out;

  nand nand_1 (nand_1_out, a3, a3);
  nand nand_2 (nand_2_out, a2, a2);
  nand nand_3 (nand_3_out, a1, a1);
  nand nand_4 (nand_4_out, a0, a0);
  _3_input_nand_gate_main main_1 (.in_1(a3), .in_2(nand_2_out), .in_3(nand_3_out), .out_4(main_1_out_4));
  _3_input_nand_gate_main main_2 (.in_1(nand_1_out), .in_2(a2), .in_3(a1), .out_4(main_2_out_4));
  nand nand_5 (nand_5_out, main_1_out_4, main_1_out_4);
  nand nand_6 (nand_6_out, main_2_out_4, main_2_out_4);
  nand nand_7 (\output , nand_5_out, nand_6_out);
endmodule
