// Logisim project lab3.circ as structural Verilog: 1 circuit, main circuit main
module main (
  input  a,
  input  b,
  input  c,
  output odd_parity,
  output even_parity
);

  wire nand_1_out, nand_2_out, nand_3_out, nand_4_out, nand_5_out, nand_6_out, nand_7_out;

  nand nand_1 (nand_1_out, a, b);
  nand nand_2 (nand_2_out, a, nand_1_out);
  nand nand_3 (nand_3_out, nand_1_out, b);
  nand nand_4 (nand_4_out, nand_2_out, nand_3_out);
  nand nand_5 (nand_5_out, nand_4_out, c);
  nand nand_6 (nand_6_out, nand_4_out, nand_5_out);
  nand nand_7 (nand_7_out, nand_5_out, c);
  nand nand_8 (even_parity, nand_6_out, nand_7_out);
  nand nand_9 (odd_parity, even_parity, even_parity);

  // Notes on the sheet:
  //   a(+)b
  //   a(+)b(+)c
  //   =(a(+)b(+)c)'
  //   =a(+)b(+)c
endmodule
