// Logisim project lab4.circ as structural Verilog: 1 circuit, main circuit main
module main (
  input  b1,
  input  a1,
  input  a0,
  input  bo,
  output c2,
  output c1,
  output c0
);

  wire main_2_carry;

  full_adder_exam_main main_1 (.a(b1), .b(a1), .carry_in(main_2_carry), .sum(c1), .carry_out(c2));
  half_adder_exam_main main_2 (.a(a0), .b(bo), .sum(c0), .carry(main_2_carry));

  // Notes on the sheet:
  //   full adder
  //   half adder
endmodule
