// Logisim project lab5.circ as structural Verilog: 1 circuit, main circuit main
module main (
  input  load,
  input  clk,
  input  reset,
  input  load_2,
  input  clk_2,
  input  reset_2,
  input  clock,
  output s0,
  output s1,
  output s2,
  output carry
);

  wire main_1_a0, main_1_a1, main_1_a2, main_2_a0, main_2_a1, main_2_a2, main_3_o0, main_3_o1, main_3_o2,
       main_4_o0, main_4_o1, main_4_o2, main_5_carry, main_6_carry_out;

  _3bitcounter_main main_1 (.load(load), .clock(clk), .reset(reset), .a2(main_1_a2), .a1(main_1_a1), .a0(main_1_a0));
  _3bitcounter_main main_2 (
    .load(load_2), .clock(clk_2), .reset(reset_2), .a2(main_2_a2), .a1(main_2_a1), .a0(main_2_a0));
  _3_bit_register_main main_3 (
    .a2(main_1_a2), .a1(main_1_a1), .a0(main_1_a0), .o0(main_3_o0), .o1(main_3_o1), .o2(main_3_o2),
    .clk(clock));
  _3_bit_register_main main_4 (
    .a2(main_2_a2), .a1(main_2_a1), .a0(main_2_a0), .o0(main_4_o0), .o1(main_4_o1), .o2(main_4_o2),
    .clk(clock));
  half_adder_exam_main main_5 (.a(main_4_o0), .b(main_3_o0), .sum(s0), .carry(main_5_carry));
  full_adder_exam_main main_6 (
    .a(main_3_o1), .b(main_4_o1), .carry_in(main_5_carry), .sum(s1), .carry_out(main_6_carry_out));
  full_adder_exam_main main_7 (.a(main_3_o2), .b(main_4_o2), .carry_in(main_6_carry_out), .sum(s2), .carry_out(carry));

  // Notes on the sheet:
  //   counter 1
  //   counter 2
  //          pipo register 1
  //   pipo register 2
  //   half adder
  //   full adder 1
  //   full adder 2
endmodule
