// Logisim project mod 100.circ as structural Verilog: 1 circuit, main circuit main
module main (
  input  in_1,
  input  in_2
);

  wire and_1_out, and_2_out, clock_1_out, main_1_a0, main_1_a1, main_1_a2, main_1_a3, main_2_a0, main_2_a1,
       main_2_a2, main_2_a3, main_3_a_2, main_3_b_2, main_3_c_2, main_3_d_2, main_3_e, main_3_f, main_3_g,
       main_4_a_2, main_4_b_2, main_4_c_2, main_4_d_2, main_4_e, main_4_f, main_4_g, multiplexer_1_out,
       not_1_out, not_2_out, not_3_out, not_4_out, not_5_out, not_6_out, not_7_out;

  Clock clock_1 (.out(clock_1_out));
  DECADE_main main_1 (
    .lode(clock_1_out), .clk(in_2), .a3(main_1_a3), .a2(main_1_a2), .a1(main_1_a1), .a0(main_1_a0),
    .reset_key(in_1));  // open: load_signal
  not not_1 (not_1_out, main_1_a1);
  not not_2 (not_2_out, main_1_a2);
  not not_3 (not_3_out, main_1_a1);
  not not_4 (not_4_out, main_1_a2);
  DECADE_main main_2 (
    .lode(multiplexer_1_out), .clk(in_2), .a3(main_2_a3), .a2(main_2_a2), .a1(main_2_a1), .a0(main_2_a0),
    .reset_key(in_1));  // open: load_signal
  not not_5 (not_5_out, in_2);
  and and_1 (and_1_out, main_1_a0, not_1_out, not_2_out, main_1_a3);
  not not_6 (not_6_out, main_1_a0);
  not not_7 (not_7_out, main_1_a3);
  and and_2 (and_2_out, not_3_out, not_6_out, not_4_out, not_7_out);
  Multiplexer #(.enable("false")) multiplexer_1 (
    .in0(and_1_out), .in1(and_2_out), .out(multiplexer_1_out), .sel(not_5_out));
  _7_segment_display_decoder_main main_3 (
    .A(main_2_a3), .B(main_2_a2), .c(main_2_a1), .D(main_2_a0), .a_2(main_3_a_2), .b_2(main_3_b_2),
    .c_2(main_3_c_2), .d_2(main_3_d_2), .e(main_3_e), .f(main_3_f), .g(main_3_g));
  _7_Segment_Display u_7_segment_display_1 (
    .g(main_3_g), .f(main_3_f), .a(main_3_a_2), .b(main_3_b_2), .e(main_3_e), .d(main_3_d_2), .c(main_3_c_2));  // open: dp
  _7_Segment_Display u_7_segment_display_2 (
    .g(main_4_g), .f(main_4_f), .a(main_4_a_2), .b(main_4_b_2), .e(main_4_e), .d(main_4_d_2), .c(main_4_c_2));  // open: dp
  _7_segment_display_decoder_main main_4 (
    .A(main_1_a3), .B(main_1_a2), .c(main_1_a1), .D(main_1_a0), .a_2(main_4_a_2), .b_2(main_4_b_2),
    .c_2(main_4_c_2), .d_2(main_4_d_2), .e(main_4_e), .f(main_4_f), .g(main_4_g));
endmodule
