// Logisim project mod 13 counter.circ as structural Verilog: 1 circuit, main circuit main
module main (
  input  clk,
  input  reset,
  output a3,
  output a2,
  output a1,
  output a0
);

  wire and_1_out, or_1_out;

  T_Flip_Flop #(.trigger("falling")) t_ff_1 (.clk(clk), .T(1'b1), .Q(a0), .preset(or_1_out));  // open: Qn, reset, en
  T_Flip_Flop #(.trigger("falling")) t_ff_2 (.clk(a0), .T(1'b1), .Q(a1), .reset(or_1_out));  // open: Qn, preset, en
  T_Flip_Flop #(.trigger("falling")) t_ff_3 (.clk(a1), .T(1'b1), .Q(a2), .reset(or_1_out));  // open: Qn, preset, en
  T_Flip_Flop #(.trigger("falling")) t_ff_4 (.clk(a2), .T(1'b1), .Q(a3), .reset(or_1_out));  // open: Qn, preset, en
  or or_1 (or_1_out, and_1_out, reset);
  and and_1 (and_1_out, a0, a2, a3);
endmodule
