// Logisim project mod 13 up.circ as structural Verilog: 1 circuit, main circuit main
module main (
  input  clk,
  input  reset,
  input  lode,
  input  [3:0] lode_bit,
  output q3,
  output q2,
  output q1,
  output q0
);

  wire and_1_out, and_2_out, and_3_out, and_4_out, multiplexer_1_out, multiplexer_2_out, multiplexer_3_out,
       multiplexer_4_out, or_1_out, or_2_out;

  and and_1 (and_1_out, q0, q1);
  and and_2 (and_2_out, q2, q3);
  T_Flip_Flop #(.trigger("falling")) t_ff_1 (
    .clk(clk), .T(multiplexer_1_out), .Q(q0), .reset(reset));  // open: Qn, preset, en
  Multiplexer #(.enable("false")) multiplexer_1 (.in0(1'b1), .in1(lode_bit[0]), .out(multiplexer_1_out), .sel(lode));
  or or_1 (or_1_out, and_1_out, and_2_out);
  Multiplexer #(.enable("false")) multiplexer_2 (.in0(q0), .in1(lode_bit[1]), .out(multiplexer_2_out), .sel(lode));
  T_Flip_Flop #(.trigger("falling")) t_ff_2 (
    .clk(clk), .T(multiplexer_2_out), .Q(q1), .reset(reset));  // open: Qn, preset, en
  and and_3 (and_3_out, q2, q3);
  and and_4 (and_4_out, q0, q1, q2);
  T_Flip_Flop #(.trigger("falling")) t_ff_3 (
    .clk(clk), .T(multiplexer_3_out), .Q(q2), .reset(reset));  // open: Qn, preset, en
  Multiplexer #(.enable("false")) multiplexer_3 (
    .in0(or_1_out), .in1(lode_bit[2]), .out(multiplexer_3_out), .sel(lode));
  or or_2 (or_2_out, and_3_out, and_4_out);
  T_Flip_Flop #(.trigger("falling")) t_ff_4 (
    .clk(clk), .T(multiplexer_4_out), .Q(q3), .reset(reset));  // open: Qn, preset, en
  Multiplexer #(.enable("false")) multiplexer_4 (
    .in0(or_2_out), .in1(lode_bit[3]), .out(multiplexer_4_out), .sel(lode));

  // Notes on the sheet:
  //   q3
  //   q2
  //   q0
  //   q1
endmodule
