// Logisim project mod 3 counter.circ as structural Verilog: 1 circuit, main circuit main
module main (
  input  [1:0] in_1,
  input  load,
  input  clock,
  input  reset,
  output q1,
  output q0
);

  wire multiplexer_1_out, multiplexer_2_out, not_1_out, or_1_out;

  Multiplexer #(.enable("false")) multiplexer_1 (.in0(not_1_out), .in1(in_1[0]), .out(multiplexer_1_out), .sel(load));
  not not_1 (not_1_out, q1);
  T_Flip_Flop #(.trigger("falling")) t_ff_1 (
    .clk(clock), .T(multiplexer_1_out), .Q(q0), .reset(reset));  // open: Qn, preset, en
  Multiplexer #(.enable("false")) multiplexer_2 (.in0(or_1_out), .in1(in_1[1]), .out(multiplexer_2_out), .sel(load));
  or or_1 (or_1_out, q0, q1);
  T_Flip_Flop #(.trigger("falling")) t_ff_2 (
    .clk(clock), .T(multiplexer_2_out), .Q(q1), .reset(reset));  // open: Qn, preset, en

  // Notes on the sheet:
  //   q1
  //   q0
endmodule
