// Logisim project mod 30 counter.circ as structural Verilog: 1 circuit, main circuit main
module main (
  input  [1:0] lode_bit_for_upper_bcd,
  input  [3:0] lode_bit_for_lower_bcd,
  input  load,
  input  reset,
  input  clock,
  output if_29,
  output if_25,
  output q1_upper,
  output q0_upper,
  output q3,
  output q2,
  output q1,
  output q0,
  output [3:0] lower_bcd,
  output [3:0] upper_bcd
);

  wire and_1_out, multiplexer_1_out, not_1_out, not_2_out, not_3_out, not_4_out, not_5_out;

  Multiplexer #(.enable("false")) multiplexer_1 (.in0(and_1_out), .in1(clock), .out(multiplexer_1_out), .sel(load));
  mod_3_counter_main main_1 (
    .load(load), .clock(multiplexer_1_out), .in_1(lode_bit_for_upper_bcd), .q1(lower_bcd[1]),
    .q0(lower_bcd[0]), .reset(reset));
  Hex_Digit_Display hex_digit_display_1 (.value({2'b00, lower_bcd[1:0]}));  // open: dp
  not not_1 (not_1_out, lower_bcd[0]);
  DECADE_main main_2 (
    .lode(load), .clk(clock), .load_signal(lode_bit_for_lower_bcd), .a3(q3), .a2(q2), .a1(q1), .a0(q0),
    .reset_key(reset));
  not not_2 (not_2_out, q2);
  not not_3 (not_3_out, q1);
  and and_1 (and_1_out, q3, not_2_out, not_3_out, q0);
  Hex_Digit_Display hex_digit_display_2 (.value({q3, q2, q1, q0}));  // open: dp
  not not_4 (not_4_out, q1);
  not not_5 (not_5_out, q3);
  and and_2 (if_29, and_1_out, not_1_out, lower_bcd[1]);
  and and_3 (if_25, not_1_out, lower_bcd[1], q2, q0, not_4_out, not_5_out);

  assign lower_bcd[3:2] = 2'b00;
  assign q0_upper = lower_bcd[0];
  assign q1_upper = lower_bcd[1];
  assign upper_bcd = {q3, q2, q1, q0};
endmodule
