// Logisim project mod 6 asyncronous counter.circ as structural Verilog: 1 circuit, main circuit main
module main (
  input  [2:0] load_signal,
  input  load,
  input  clock,
  input  reset,
  output out_5,
  output out_6,
  output out_7
);

  wire and_1_out, and_2_out, and_3_out, multiplexer_1_out, multiplexer_2_out, multiplexer_3_out, not_1_out,
       or_1_out, or_2_out;

  Multiplexer #(.enable("false")) multiplexer_1 (.in0(1'b1), .in1(load_signal[0]), .out(multiplexer_1_out), .sel(load));
  Multiplexer #(.enable("false")) multiplexer_2 (
    .in0(or_1_out), .in1(load_signal[1]), .out(multiplexer_2_out), .sel(load));
  T_Flip_Flop #(.trigger("falling")) t_ff_1 (
    .clk(clock), .T(multiplexer_1_out), .Q(out_7), .reset(reset));  // open: Qn, preset, en
  Multiplexer #(.enable("false")) multiplexer_3 (
    .in0(or_2_out), .in1(load_signal[2]), .out(multiplexer_3_out), .sel(load));
  T_Flip_Flop #(.trigger("falling")) t_ff_2 (
    .clk(clock), .T(multiplexer_2_out), .Q(out_6), .reset(reset));  // open: Qn, preset, en
  and and_1 (and_1_out, out_6, out_7);
  T_Flip_Flop #(.trigger("falling")) t_ff_3 (
    .clk(clock), .T(multiplexer_3_out), .Q(out_5), .reset(reset));  // open: Qn, preset, en
  not not_1 (not_1_out, out_5);
  and and_2 (and_2_out, out_7, out_5);
  and and_3 (and_3_out, out_7, not_1_out);
  or or_1 (or_1_out, and_1_out, and_3_out);
  or or_2 (or_2_out, and_2_out, and_1_out);
endmodule
