// Logisim project mod 60 countre.circ as structural Verilog: 1 circuit, main circuit main
module main (
  input  [2:0] mod6,
  input  [3:0] mod10,
  input  reset,
  input  load,
  input  clk,
  output lower_bcd_a0,
  output lower_bcd_a1,
  output lower_bcd_a2,
  output lower_bcd_a3,
  output if_59,
  output [3:0] lower_bcd,
  output upper_bcd_a4,
  output uppre_bcd_a5,
  output upper_bcd_a6,
  output upper_bcd_a7,
  output [3:0] upper_bcd,
  output if_55
);

  wire and_1_out, main_2_a_2, main_2_b_2, main_2_c_2, main_2_d_2, main_2_e, main_2_f, main_2_g, main_4_a_2,
       main_4_b_2, main_4_c_2, main_4_d_2, main_4_e, main_4_f, main_4_g, multiplexer_1_out, not_1_out,
       not_2_out, not_3_out, not_4_out, not_5_out, not_6_out, not_7_out, not_8_out, not_9_out, not_10_out;

  DECADE_main main_1 (
    .lode(load), .clk(clk), .load_signal(mod10), .a3(lower_bcd[3]), .a2(lower_bcd[2]), .a1(lower_bcd[1]),
    .a0(lower_bcd[0]), .reset_key(reset));
  _7_segment_display_decoder_main main_2 (
    .A(lower_bcd[3]), .B(lower_bcd[2]), .c(lower_bcd[1]), .D(lower_bcd[0]), .a_2(main_2_a_2),
    .b_2(main_2_b_2), .c_2(main_2_c_2), .d_2(main_2_d_2), .e(main_2_e), .f(main_2_f), .g(main_2_g));
  not not_1 (not_1_out, lower_bcd[1]);
  not not_2 (not_2_out, lower_bcd[2]);
  Multiplexer #(.enable("false")) multiplexer_1 (.in0(and_1_out), .in1(clk), .out(multiplexer_1_out), .sel(load));
  and and_1 (and_1_out, lower_bcd[0], not_1_out, not_2_out, lower_bcd[3]);
  mod_6_asyncronous_counter_main main_3 (
    .load_signal(mod6), .load(load), .clock(multiplexer_1_out), .out_5(upper_bcd[2]), .out_6(upper_bcd[1]),
    .out_7(upper_bcd[0]), .reset(reset));
  _7_segment_display_decoder_main main_4 (
    .A(1'b0), .B(upper_bcd[2]), .c(upper_bcd[1]), .D(upper_bcd[0]), .a_2(main_4_a_2), .b_2(main_4_b_2),
    .c_2(main_4_c_2), .d_2(main_4_d_2), .e(main_4_e), .f(main_4_f), .g(main_4_g));
  _7_Segment_Display u_7_segment_display_1 (
    .g(main_4_g), .f(main_4_f), .a(main_4_a_2), .b(main_4_b_2), .e(main_4_e), .d(main_4_d_2), .c(main_4_c_2));  // open: dp
  _7_Segment_Display u_7_segment_display_2 (
    .g(main_2_g), .f(main_2_f), .a(main_2_a_2), .b(main_2_b_2), .e(main_2_e), .d(main_2_d_2), .c(main_2_c_2));  // open: dp
  not not_3 (not_3_out, lower_bcd[1]);
  not not_4 (not_4_out, lower_bcd[2]);
  not not_5 (not_5_out, upper_bcd[1]);
  not not_6 (not_6_out, 1'b0);
  not not_7 (not_7_out, 1'b0);
  not not_8 (not_8_out, lower_bcd[1]);
  not not_9 (not_9_out, lower_bcd[3]);
  not not_10 (not_10_out, upper_bcd[1]);
  and and_2 (if_59, lower_bcd[0], not_3_out, not_4_out, lower_bcd[3], upper_bcd[0], not_5_out, upper_bcd[2], not_6_out);
  and and_3 (if_55, not_7_out, upper_bcd[2], not_10_out, upper_bcd[0], not_9_out, lower_bcd[2], not_8_out, lower_bcd[0]);

  assign lower_bcd_a0 = lower_bcd[0];
  assign lower_bcd_a1 = lower_bcd[1];
  assign lower_bcd_a2 = lower_bcd[2];
  assign lower_bcd_a3 = lower_bcd[3];
  assign upper_bcd[3] = 1'b0;
  assign upper_bcd_a4 = upper_bcd[0];
  assign upper_bcd_a6 = upper_bcd[2];
  assign upper_bcd_a7 = 1'b0;
  assign uppre_bcd_a5 = upper_bcd[1];
endmodule
