// Logisim project mod-6 counter.circ as structural Verilog: 1 circuit, main circuit main
module main (
  input  in_1,
  input  clk,
  input  reset,
  output a2,
  output a1,
  output a0
);

  wire nand_1_out, nand_2_out, nand_3_out, or_1_out, or_2_out, or_3_out;

  J_K_Flip_Flop #(.trigger("falling")) j_k_ff_1 (
    .J(in_1), .clk(clk), .K(in_1), .Q(a0), .reset(or_3_out));  // open: Qn, preset, en
  J_K_Flip_Flop #(.trigger("falling")) j_k_ff_2 (
    .J(in_1), .clk(a0), .K(in_1), .Q(a1), .reset(or_2_out));  // open: Qn, preset, en
  J_K_Flip_Flop #(.trigger("falling")) j_k_ff_3 (
    .J(in_1), .clk(a1), .K(in_1), .Q(a2), .reset(or_1_out));  // open: Qn, preset, en
  nand nand_1 (nand_1_out, a0, a0);
  or or_1 (or_1_out, reset, nand_3_out);
  or or_2 (or_2_out, reset, nand_3_out);
  or or_3 (or_3_out, nand_3_out, reset);
  nand nand_2 (nand_2_out, a1, nand_1_out, a2);
  nand nand_3 (nand_3_out, nand_2_out, nand_2_out);
endmodule
