// Logisim project multiplexer.circ as structural Verilog: 1 circuit, main circuit main
module main (
  input  i0,
  input  i1,
  input  i2,
  input  i3,
  input  s0,
  input  s1,
  output out_7
);

  wire and_1_out, and_2_out, and_3_out, and_4_out, not_1_out, not_2_out;

  not not_1 (not_1_out, s0);
  not not_2 (not_2_out, s1);
  buf and_1 (and_1_out, not_1_out);  // AND_Gate
  and and_2 (and_2_out, not_1_out, s1, i1);
  and and_3 (and_3_out, s0, not_2_out, i2);
  and and_4 (and_4_out, s1, s0, i3);
  or or_1 (out_7, and_1_out, and_2_out, and_3_out, and_4_out);
endmodule
