// Logisim project sirial adder.circ as structural Verilog: 1 circuit, main circuit main
module main (
  input  in_1,
  input  in_2,
  input  in_3,
  input  in_4,
  input  in_5,
  input  in_6,
  input  in_7,
  input  in_8,
  input  in_9,
  output s2,
  output s1,
  output s0,
  output carry_out
);

  wire clock_1_out, clock_2_out, clock_3_out, d_ff_1_q, main_1_a0, main_1_a1, main_1_a2, main_2_a0,
       main_2_a1, main_2_a2, main_3_output, main_4_output, main_5_sum;

  Clock clock_1 (.out(clock_1_out));
  Clock clock_2 (.out(clock_2_out));
  _3bitcounter_main main_1 (
    .load(in_1), .clock(clock_1_out), .reset(in_4), .a2(main_1_a2), .a1(main_1_a1), .a0(main_1_a0));
  _3bitcounter_main main_2 (
    .load(in_5), .clock(clock_2_out), .reset(in_7), .a2(main_2_a2), .a1(main_2_a1), .a0(main_2_a0));
  Clock clock_3 (.out(clock_3_out));
  _3_bit_parallel_in_sirial_out_shift_register_main main_3 (
    .shift(in_9), .clk(clock_3_out), .rst(in_3), .a2(main_1_a2), .a1(main_1_a1), .a0(main_1_a0),
    .\output (main_3_output));
  _3_bit_parallel_in_sirial_out_shift_register_main main_4 (
    .shift(in_9), .clk(clock_3_out), .rst(in_6), .a2(main_2_a2), .a1(main_2_a1), .a0(main_2_a0),
    .\output (main_4_output));
  full_adder_exam_main main_5 (
    .a(main_3_output), .b(main_4_output), .carry_in(d_ff_1_q), .sum(main_5_sum), .carry_out(carry_out));
  D_Flip_Flop d_ff_1 (.clk(clock_3_out), .D(carry_out), .Q(d_ff_1_q), .reset(in_8));  // open: Qn, preset, en
  _3_bit_sirial_in_parallel_out_register_main main_6 (
    .\input (main_5_sum), .clock(clock_3_out), .reset(in_2), .s2(s2), .s1(s1), .s0(s0));

  // Notes on the sheet:
  //   counter 1
  //   counter 2
  //   piso register 1
  //   piso register 2
  //   3-bit serial adder taking inputs from counters and output store at SIPO register
  //   full adder
  //   sipo register
endmodule
