// Logisim project time clock for signal.circ as structural Verilog: 1 circuit, main circuit main
module main (
  input  reset,
  input  to_pm,
  input  clock,
  input  load,
  input  [3:0] hour,
  input  [3:0] second_1,
  input  [2:0] second_2,
  input  [2:0] minute_2,
  input  [3:0] minute_1,
  output [3:0] hour_2,
  output [3:0] hour_1,
  output [3:0] minute_2_2,
  output [3:0] second_2_2,
  output [3:0] second_1_2,
  output [3:0] minute_1_2,
  output if_am_pm
);

  wire and_1_out, main_2_q0, main_2_q1, main_2_q2, main_2_q3, main_3_if_59, main_4_if_59, multiplexer_1_out,
       multiplexer_2_out, not_1_out, not_2_out;

  binary_to_bcd_encoader_main main_1 (
    .A(main_2_q3), .B(main_2_q2), .C(main_2_q1), .D(main_2_q0), .b8(hour_2[3]), .b7(hour_2[2]),
    .b6(hour_2[1]), .b5(hour_2[0]), .b4(hour_1[3]), .b3(hour_1[2]), .b2(hour_1[1]), .b1(hour_1[0]));
  mod_13_up_main main_2 (
    .clk(multiplexer_1_out), .lode(load), .lode_bit(hour), .q3(main_2_q3), .q2(main_2_q2), .q1(main_2_q1),
    .q0(main_2_q0), .reset(reset));
  mod_60_countre_main main_3 (
    .load(load), .clk(multiplexer_2_out), .mod6(minute_2), .mod10(minute_1), .if_59(main_3_if_59),
    .lower_bcd_a0(minute_1_2[0]), .lower_bcd_a1(minute_1_2[1]), .lower_bcd_a2(minute_1_2[2]),
    .lower_bcd_a3(minute_1_2[3]), .reset(reset), .upper_bcd_a4(minute_2_2[0]), .uppre_bcd_a5(minute_2_2[1]),
    .upper_bcd_a6(minute_2_2[2]), .upper_bcd_a7(minute_2_2[3]));  // open: lower_bcd, upper_bcd, if_55
  not not_1 (not_1_out, main_2_q1);
  not not_2 (not_2_out, main_2_q0);
  Hex_Digit_Display hex_digit_display_1 (.value(hour_2));  // open: dp
  Hex_Digit_Display hex_digit_display_2 (.value(hour_1), .dp(1'b1));
  Multiplexer #(.enable("false")) multiplexer_1 (.in0(main_3_if_59), .in1(clock), .out(multiplexer_1_out), .sel(load));
  Hex_Digit_Display hex_digit_display_3 (.value(minute_2_2));  // open: dp
  Multiplexer #(.enable("false")) multiplexer_2 (.in0(main_4_if_59), .in1(clock), .out(multiplexer_2_out), .sel(load));
  Hex_Digit_Display hex_digit_display_4 (.value(minute_1_2), .dp(1'b1));
  Hex_Digit_Display hex_digit_display_5 (.value(second_2_2));  // open: dp
  mod_60_countre_main main_4 (
    .load(load), .clk(clock), .mod6(second_2), .mod10(second_1), .if_59(main_4_if_59),
    .lower_bcd_a0(second_1_2[0]), .lower_bcd_a1(second_1_2[1]), .lower_bcd_a2(second_1_2[2]),
    .lower_bcd_a3(second_1_2[3]), .reset(reset), .upper_bcd_a4(second_2_2[0]), .uppre_bcd_a5(second_2_2[1]),
    .upper_bcd_a6(second_2_2[2]), .upper_bcd_a7(second_2_2[3]));  // open: lower_bcd, upper_bcd, if_55
  Hex_Digit_Display hex_digit_display_6 (.value(second_1_2));  // open: dp
  and and_1 (and_1_out, main_2_q3, main_2_q2, not_1_out, not_2_out);
  _7_Segment_Display u_7_segment_display_1 (
    .g(1'b1), .f(1'b1), .a(1'b1), .b(1'b1), .e(1'b1), .c(if_am_pm));  // open: d, dp
  DotMatrix #(.matrixcols(7)) dotmatrix_1 (
    .col0({7{1'b1}}), .col1(7'b0100000), .col2(7'b0010000), .col3(7'b0001000), .col4(7'b0010000),
    .col5(7'b0100000), .col6({7{1'b1}}));
  T_Flip_Flop t_ff_1 (.clk(and_1_out), .T(1'b1), .Q(if_am_pm), .preset(reset), .reset(to_pm));  // open: Qn, en
endmodule
