// Logisim project time clock.circ as structural Verilog: 1 circuit, main circuit main
module main (
  input  in_1,
  input  in_2,
  input  [3:0] hour,
  input  [2:0] in_4,
  input  [3:0] in_5,
  input  [2:0] in_6,
  input  [3:0] seconds
);

  wire and_1_out, clock_1_out, main_1_b1, main_1_b2, main_1_b3, main_1_b4, main_1_b5, main_1_b6, main_1_b7,
       main_1_b8, main_2_a_2, main_2_b_2, main_2_c_2, main_2_d_2, main_2_e, main_2_f, main_2_g, main_3_q0,
       main_3_q1, main_3_q2, main_3_q3, main_4_a_2, main_4_b_2, main_4_c_2, main_4_d_2, main_4_e, main_4_f,
       main_4_g, main_5_if_59, main_5_lower_bcd_a0, main_5_lower_bcd_a1, main_5_lower_bcd_a2,
       main_5_lower_bcd_a3, main_5_upper_bcd_a4, main_5_upper_bcd_a6, main_5_upper_bcd_a7,
       main_5_uppre_bcd_a5, main_6_a_2, main_6_b_2, main_6_c_2, main_6_d_2, main_6_e, main_6_f, main_6_g,
       main_7_a_2, main_7_b_2, main_7_c_2, main_7_d_2, main_7_e, main_7_f, main_7_g, main_8_if_59,
       main_8_lower_bcd_a0, main_8_lower_bcd_a1, main_8_lower_bcd_a2, main_8_lower_bcd_a3,
       main_8_upper_bcd_a4, main_8_upper_bcd_a6, main_8_upper_bcd_a7, main_8_uppre_bcd_a5, main_9_a_2,
       main_9_b_2, main_9_c_2, main_9_d_2, main_9_e, main_9_f, main_9_g, main_10_a_2, main_10_b_2,
       main_10_c_2, main_10_d_2, main_10_e, main_10_f, main_10_g, multiplexer_1_out, multiplexer_2_out,
       not_1_out, not_2_out, t_ff_1_q;

  binary_to_bcd_encoader_main main_1 (
    .A(main_3_q3), .B(main_3_q2), .C(main_3_q1), .D(main_3_q0), .b8(main_1_b8), .b7(main_1_b7),
    .b6(main_1_b6), .b5(main_1_b5), .b4(main_1_b4), .b3(main_1_b3), .b2(main_1_b2), .b1(main_1_b1));
  _7_segment_display_decoder_main main_2 (
    .A(main_1_b8), .B(main_1_b7), .c(main_1_b6), .D(main_1_b5), .a_2(main_2_a_2), .b_2(main_2_b_2),
    .c_2(main_2_c_2), .d_2(main_2_d_2), .e(main_2_e), .f(main_2_f), .g(main_2_g));
  mod_13_up_main main_3 (
    .clk(multiplexer_1_out), .lode(in_2), .lode_bit(hour), .q3(main_3_q3), .q2(main_3_q2), .q1(main_3_q1),
    .q0(main_3_q0), .reset(in_1));
  _7_segment_display_decoder_main main_4 (
    .A(main_1_b4), .B(main_1_b3), .c(main_1_b2), .D(main_1_b1), .a_2(main_4_a_2), .b_2(main_4_b_2),
    .c_2(main_4_c_2), .d_2(main_4_d_2), .e(main_4_e), .f(main_4_f), .g(main_4_g));
  mod_60_countre_main main_5 (
    .load(in_2), .clk(multiplexer_2_out), .mod6(in_4), .mod10(in_5), .if_59(main_5_if_59),
    .lower_bcd_a0(main_5_lower_bcd_a0), .lower_bcd_a1(main_5_lower_bcd_a1),
    .lower_bcd_a2(main_5_lower_bcd_a2), .lower_bcd_a3(main_5_lower_bcd_a3), .reset(in_1),
    .upper_bcd_a4(main_5_upper_bcd_a4), .uppre_bcd_a5(main_5_uppre_bcd_a5),
    .upper_bcd_a6(main_5_upper_bcd_a6), .upper_bcd_a7(main_5_upper_bcd_a7));  // open: lower_bcd, upper_bcd, if_55
  _7_Segment_Display u_7_segment_display_1 (
    .g(main_2_g), .f(main_2_f), .a(main_2_a_2), .b(main_2_b_2), .e(main_2_e), .d(main_2_d_2), .c(main_2_c_2));  // open: dp
  not not_1 (not_1_out, main_3_q1);
  not not_2 (not_2_out, main_3_q0);
  _7_segment_display_decoder_main main_6 (
    .A(main_5_upper_bcd_a7), .B(main_5_upper_bcd_a6), .c(main_5_uppre_bcd_a5), .D(main_5_upper_bcd_a4),
    .a_2(main_6_a_2), .b_2(main_6_b_2), .c_2(main_6_c_2), .d_2(main_6_d_2), .e(main_6_e), .f(main_6_f),
    .g(main_6_g));
  _7_Segment_Display u_7_segment_display_2 (
    .g(main_4_g), .f(main_4_f), .a(main_4_a_2), .b(main_4_b_2), .e(main_4_e), .d(main_4_d_2), .c(main_4_c_2),
    .dp(1'b1));
  Clock clock_1 (.out(clock_1_out));
  _7_segment_display_decoder_main main_7 (
    .A(main_5_lower_bcd_a3), .B(main_5_lower_bcd_a2), .c(main_5_lower_bcd_a1), .D(main_5_lower_bcd_a0),
    .a_2(main_7_a_2), .b_2(main_7_b_2), .c_2(main_7_c_2), .d_2(main_7_d_2), .e(main_7_e), .f(main_7_f),
    .g(main_7_g));
  Multiplexer #(.enable("false")) multiplexer_1 (
    .in0(main_5_if_59), .in1(clock_1_out), .out(multiplexer_1_out), .sel(in_2));
  _7_Segment_Display u_7_segment_display_3 (
    .g(main_6_g), .f(main_6_f), .a(main_6_a_2), .b(main_6_b_2), .e(main_6_e), .d(main_6_d_2), .c(main_6_c_2));  // open: dp
  _7_Segment_Display u_7_segment_display_4 (
    .g(main_7_g), .f(main_7_f), .a(main_7_a_2), .b(main_7_b_2), .e(main_7_e), .d(main_7_d_2), .c(main_7_c_2),
    .dp(1'b1));
  Multiplexer #(.enable("false")) multiplexer_2 (
    .in0(main_8_if_59), .in1(clock_1_out), .out(multiplexer_2_out), .sel(in_2));
  _7_Segment_Display u_7_segment_display_5 (
    .g(main_9_g), .f(main_9_f), .a(main_9_a_2), .b(main_9_b_2), .e(main_9_e), .d(main_9_d_2), .c(main_9_c_2));  // open: dp
  mod_60_countre_main main_8 (
    .load(in_2), .clk(clock_1_out), .mod6(in_6), .mod10(seconds), .if_59(main_8_if_59),
    .lower_bcd_a0(main_8_lower_bcd_a0), .lower_bcd_a1(main_8_lower_bcd_a1),
    .lower_bcd_a2(main_8_lower_bcd_a2), .lower_bcd_a3(main_8_lower_bcd_a3), .reset(in_1),
    .upper_bcd_a4(main_8_upper_bcd_a4), .uppre_bcd_a5(main_8_uppre_bcd_a5),
    .upper_bcd_a6(main_8_upper_bcd_a6), .upper_bcd_a7(main_8_upper_bcd_a7));  // open: lower_bcd, upper_bcd, if_55
  _7_Segment_Display u_7_segment_display_6 (
    .g(main_10_g), .f(main_10_f), .a(main_10_a_2), .b(main_10_b_2), .e(main_10_e), .d(main_10_d_2),
    .c(main_10_c_2));  // open: dp
  and and_1 (and_1_out, main_3_q3, main_3_q2, not_1_out, not_2_out);
  _7_segment_display_decoder_main main_9 (
    .A(main_8_upper_bcd_a7), .B(main_8_upper_bcd_a6), .c(main_8_uppre_bcd_a5), .D(main_8_upper_bcd_a4),
    .a_2(main_9_a_2), .b_2(main_9_b_2), .c_2(main_9_c_2), .d_2(main_9_d_2), .e(main_9_e), .f(main_9_f),
    .g(main_9_g));
  _7_Segment_Display u_7_segment_display_7 (
    .g(1'b1), .f(1'b1), .a(1'b1), .b(1'b1), .e(1'b1), .c(t_ff_1_q));  // open: d, dp
  _7_segment_display_decoder_main main_10 (
    .A(main_8_lower_bcd_a3), .B(main_8_lower_bcd_a2), .c(main_8_lower_bcd_a1), .D(main_8_lower_bcd_a0),
    .a_2(main_10_a_2), .b_2(main_10_b_2), .c_2(main_10_c_2), .d_2(main_10_d_2), .e(main_10_e), .f(main_10_f),
    .g(main_10_g));
  DotMatrix #(.matrixcols(7)) dotmatrix_1 (
    .col0({7{1'b1}}), .col1(7'b0100000), .col2(7'b0010000), .col3(7'b0001000), .col4(7'b0010000),
    .col5(7'b0100000), .col6({7{1'b1}}));
  T_Flip_Flop t_ff_1 (.clk(and_1_out), .T(1'b1), .Q(t_ff_1_q), .preset(in_1));  // open: Qn, reset, en

  // Notes on the sheet:
  //   minutes
endmodule
