// Logisim project traffic signal.circ as structural Verilog: 1 circuit, main circuit main
module main (
  input  in_1,
  input  in_2,
  input  in_3,
  input  [3:0] in_4,
  input  [2:0] in_5,
  input  [3:0] in_6,
  input  [2:0] in_7,
  input  [3:0] in_8,
  input  in_9,
  input  in_10,
  input  in_11,
  input  in_12
);

  wire and_1_out, and_2_out, and_3_out, and_4_out, and_5_out, and_6_out, and_7_out, clock_1_out,
       demultiplexer_1_out0, demultiplexer_1_out1, main_1_if_55, main_1_if_59, main_3_if_25, main_3_if_29,
       main_4_if_am_pm, multiplexer_1_out, multiplexer_2_out, not_1_out, not_2_out, not_3_out, not_4_out,
       not_5_out, not_6_out, not_7_out, not_8_out, or_1_out, or_2_out, or_3_out, or_4_out, or_5_out,
       or_6_out, t_ff_1_q, t_ff_2_q, t_ff_3_q, t_ff_4_q;
  wire [2:0] main_2_out_7, multiplexer_11_out_2;
  wire [3:0] main_1_lower_bcd, main_1_upper_bcd, main_3_lower_bcd, main_3_upper_bcd, main_4_hour_1,
       main_4_hour_2, main_4_minute_1_2, main_4_minute_2_2, main_4_second_1_2, main_4_second_2_2,
       multiplexer_3_out, multiplexer_4_out;
  wire [20:0] multiplexer_11_out;
  wire [23:0] multiplexer_5_out, multiplexer_6_out, multiplexer_7_out, multiplexer_8_out, multiplexer_9_out,
       multiplexer_10_out;

  Clock clock_1 (.out(clock_1_out));
  Demultiplexer #(.enable("false")) demultiplexer_1 (
    .out0(demultiplexer_1_out0), .out1(demultiplexer_1_out1), .in(clock_1_out), .sel(and_7_out));
  Multiplexer #(.enable("false")) multiplexer_1 (
    .in0(main_3_if_29), .in1(main_1_if_59), .out(multiplexer_1_out), .sel(and_7_out));
  or or_1 (or_1_out, multiplexer_1_out, multiplexer_2_out);
  mod_60_countre_main main_1 (
    .load(in_11), .clk(demultiplexer_1_out1), .if_59(main_1_if_59), .lower_bcd(main_1_lower_bcd),
    .upper_bcd(main_1_upper_bcd), .if_55(main_1_if_55));  // open: mod6, mod10, lower_bcd_a0, lower_bcd_a1, lower_bcd_a2, lower_bcd_a3, reset, upper_bcd_a4, uppre_bcd_a5, upper_bcd_a6, upper_bcd_a7
  mod_6_asyncronous_counter_main main_2 (
    .load(in_2), .clock(multiplexer_1_out), .out_5(main_2_out_7[2]), .out_6(main_2_out_7[1]),
    .out_7(main_2_out_7[0]), .reset(in_1));  // open: load_signal
  not not_1 (not_1_out, main_2_out_7[2]);
  not not_2 (not_2_out, main_2_out_7[1]);
  Multiplexer #(.enable("false")) multiplexer_2 (
    .in0(main_3_if_25), .in1(main_1_if_55), .out(multiplexer_2_out), .sel(and_7_out));
  mod_30_counter_main main_3 (
    .load(in_3), .clock(demultiplexer_1_out0), .if_29(main_3_if_29), .if_25(main_3_if_25),
    .lower_bcd(main_3_lower_bcd), .upper_bcd(main_3_upper_bcd), .reset(in_1));  // open: lode_bit_for_upper_bcd, lode_bit_for_lower_bcd, q1_upper, q0_upper, q3, q2, q1, q0
  T_Flip_Flop #(.trigger("falling")) t_ff_1 (
    .clk(or_1_out), .T(1'b1), .Q(t_ff_1_q), .reset(in_1));  // open: Qn, preset, en
  Hex_Digit_Display hex_digit_display_1 (.value(multiplexer_3_out));  // open: dp
  or or_2 (or_2_out, clock_1_out, in_12);
  and and_1 (and_1_out, not_1_out, main_2_out_7[1], main_2_out_7[0]);
  or or_3 (or_3_out, and_1_out, and_2_out);
  and and_2 (and_2_out, main_2_out_7[2], not_2_out, main_2_out_7[0]);
  Hex_Digit_Display hex_digit_display_2 (.value(multiplexer_4_out));  // open: dp
  T_Flip_Flop #(.trigger("falling")) t_ff_2 (
    .clk(or_3_out), .T(1'b1), .Q(t_ff_2_q), .reset(in_1));  // open: Qn, preset, en
  LED led_1 (.in(multiplexer_11_out[0]));
  LED led_2 (.in(multiplexer_11_out_2[2]));
  time_clock_for_signal_main main_4 (
    .clock(or_2_out), .load(in_10), .hour(in_4), .minute_2(in_5), .minute_1(in_6), .second_2(in_7),
    .second_1(in_8), .hour_2(main_4_hour_2), .hour_1(main_4_hour_1), .minute_2_2(main_4_minute_2_2),
    .minute_1_2(main_4_minute_1_2), .second_2_2(main_4_second_2_2), .second_1_2(main_4_second_1_2),
    .if_am_pm(main_4_if_am_pm), .reset(in_1), .to_pm(in_9));
  not not_3 (not_3_out, main_4_hour_2[0]);
  LED led_3 (.in(multiplexer_11_out[5]));
  LED led_4 (.in(multiplexer_11_out[4]));
  LED led_5 (.in(multiplexer_11_out[3]));
  LED led_6 (.in(multiplexer_11_out[1]));
  LED led_7 (.in(multiplexer_11_out[2]));
  LED led_8 (.in(multiplexer_11_out_2[1]));
  LED led_9 (.in(multiplexer_11_out_2[0]));
  Multiplexer #(.width(4), .enable("false")) multiplexer_3 (
    .in0(main_3_lower_bcd), .in1(main_1_upper_bcd), .out(multiplexer_3_out), .sel(and_7_out));
  Multiplexer #(.width(4), .enable("false")) multiplexer_4 (
    .in0(main_3_upper_bcd), .in1(main_1_lower_bcd), .out(multiplexer_4_out), .sel(and_7_out));
  not not_4 (not_4_out, main_4_hour_1[3]);
  not not_5 (not_5_out, main_4_hour_1[2]);
  LED led_10 (.in(multiplexer_11_out[6]));
  LED led_11 (.in(multiplexer_11_out[7]));
  LED led_12 (.in(multiplexer_11_out[8]));
  LED led_13 (.in(multiplexer_11_out[20]));
  LED led_14 (.in(multiplexer_11_out[19]));
  LED led_15 (.in(multiplexer_11_out[18]));
  not not_6 (not_6_out, main_4_hour_1[1]);
  not not_7 (not_7_out, main_4_if_am_pm);
  not not_8 (not_8_out, main_4_hour_1[0]);
  LED led_16 (.in(multiplexer_11_out[10]));
  LED led_17 (.in(multiplexer_11_out[9]));
  LED led_18 (.in(multiplexer_11_out[13]));
  LED led_19 (.in(multiplexer_11_out[14]));
  LED led_20 (.in(multiplexer_11_out[15]));
  LED led_21 (.in(multiplexer_11_out[16]));
  LED led_22 (.in(multiplexer_11_out[17]));
  Hex_Digit_Display hex_digit_display_3 (.value(main_4_hour_2));  // open: dp
  LED led_23 (.in(multiplexer_11_out[11]));
  LED led_24 (.in(multiplexer_11_out[12]));
  Hex_Digit_Display hex_digit_display_4 (.value(main_4_hour_1));  // open: dp
  and and_3 (and_3_out, main_4_if_am_pm, main_4_hour_1[3], not_5_out, not_6_out, not_8_out, not_3_out);
  and and_4 (and_4_out, main_4_if_am_pm, not_8_out, not_6_out, not_5_out, not_4_out, main_4_hour_2[0]);
  and and_5 (and_5_out, not_7_out, not_8_out, not_6_out, main_4_hour_1[2], not_4_out, not_3_out);
  and and_6 (and_6_out, not_7_out, not_8_out, main_4_hour_1[1], main_4_hour_1[2], not_4_out, not_3_out);
  Hex_Digit_Display hex_digit_display_5 (.value(main_4_minute_2_2));  // open: dp
  Hex_Digit_Display hex_digit_display_6 (.value(main_4_minute_1_2));  // open: dp
  or or_4 (or_4_out, and_3_out, and_4_out);
  or or_5 (or_5_out, and_5_out, and_6_out);
  Hex_Digit_Display hex_digit_display_7 (.value(main_4_second_2_2));  // open: dp
  Hex_Digit_Display hex_digit_display_8 (.value(main_4_second_1_2));  // open: dp
  T_Flip_Flop #(.trigger("falling")) t_ff_3 (.clk(or_4_out), .T(1'b1), .Q(t_ff_3_q));  // open: Qn, preset, reset, en
  T_Flip_Flop #(.trigger("falling")) t_ff_4 (.clk(or_5_out), .T(1'b1), .Q(t_ff_4_q));  // open: Qn, preset, reset, en
  Multiplexer #(.width(24), .enable("false")) multiplexer_5 (
    .in0(24'h8a4524), .in1(24'h84c321), .out(multiplexer_5_out), .sel(t_ff_1_q));
  Multiplexer #(.width(24), .enable("false")) multiplexer_6 (
    .in0(24'h914922), .in1(24'h30c861), .out(multiplexer_6_out), .sel(t_ff_1_q));
  Multiplexer #(.width(24), .enable("false")) multiplexer_7 (
    .in0(24'h5248a4), .in1(24'h32104c), .out(multiplexer_7_out), .sel(t_ff_1_q));
  Multiplexer #(.width(24), .enable("false")) multiplexer_8 (
    .in0(24'h922914), .in1(24'h321309), .out(multiplexer_8_out), .sel(t_ff_1_q));
  Multiplexer #(.width(24), .enable("false")) multiplexer_9 (
    .in0(24'h522522), .in1(24'h249249), .out(multiplexer_9_out), .sel(t_ff_1_q));
  _7_Segment_Display u_7_segment_display_1 (
    .g(1'b1), .f(1'b1), .a(1'b1), .b(1'b1), .e(1'b1), .c(main_4_if_am_pm));  // open: d, dp
  and and_7 (and_7_out, t_ff_2_q, or_6_out);
  or or_6 (or_6_out, t_ff_3_q, t_ff_4_q);
  Multiplexer #(.width(24), .enable("false")) multiplexer_10 (
    .in0(24'h894894), .in1(24'h84c24c), .out(multiplexer_10_out), .sel(t_ff_1_q));
  Multiplexer #(.select(3), .width(24), .enable("false")) multiplexer_11 (
    .in0(multiplexer_5_out), .in1(multiplexer_6_out), .in2(multiplexer_7_out), .in3(multiplexer_8_out),
    .in4(multiplexer_9_out), .in5(multiplexer_10_out), .out({multiplexer_11_out_2, multiplexer_11_out}),
    .sel(main_2_out_7));  // open: in6, in7

  // Notes on the sheet:
  //   8
  //   1
  //   7
  //   1
  //   6
  //   2
  //   0
  //   1
  //   2
  //   3
  //   5
  //   4
  //   3
  //   4
  //   5
  //   6
  //   7
  //   8
  //   11
  //   10
  //   9
  //   M
endmodule
